# Fritzing sketch Zero Delay (saved by Fritzing 0.9.5d)
circuit board: 9.42cm x 7.13126cm

parts:
  2P/4B = female pin header, 2 pins [form="♀ (female)"]
  SELECT = female pin header, 2 pins [form="♀ (female)"]
  RIGHT = female pin header, 2 pins [form="♀ (female)"]
  A1/HOME = female pin header, 2 pins [form="♀ (female)"]
  4P/L1 = female pin header, 2 pins [form="♀ (female)"]
  3P/R1 = female pin header, 2 pins [form="♀ (female)"]
  RS/TOOGLE = female pin header, 2 pins [form="♀ (female)"]
  OLED/SCL = female pin header, 2 pins [form="♀ (female)"]
  OLED/SDA = female pin header, 2 pins [form="♀ (female)"]
  TURBO/LED = female pin header, 2 pins [form="♀ (female)"]
  BOARD/RGB-LEDS = female pin header, 2 pins [form="♀ (female)"]
  4K/L2 = female pin header, 2 pins [form="♀ (female)"]
  3K/R2 = female pin header, 2 pins [form="♀ (female)"]
  Mod1 = Raspberry Pi Pico
  LEFT = female pin header, 2 pins [form="♀ (female)"]
  START = female pin header, 2 pins [form="♀ (female)"]
  2K/B2 = female pin header, 2 pins [form="♀ (female)"]
  1K/B1 = female pin header, 2 pins [form="♀ (female)"]
  UP = female pin header, 2 pins [form="♀ (female)"]
  R3/RS = female pin header, 2 pins [form="♀ (female)"]
  LS/TOOGLE = female pin header, 2 pins [form="♀ (female)"]
  1P/3B = female pin header, 2 pins [form="♀ (female)"]
  DOWN = female pin header, 2 pins [form="♀ (female)"]
  TURBO = female pin header, 2 pins [form="♀ (female)"]
  SELECT_2 = female pin header, 2 pins [form="♀ (female)"]
  A2-TP/CAPTURE = female pin header, 2 pins [form="♀ (female)"]

nets:
  N1: 2P/4B.pin1, SELECT.pin2, RIGHT.pin1, A1/HOME.pin2, 4P/L1.pin1, 3P/R1.pin1, RS/TOOGLE.pin2, OLED/SCL.pin1, OLED/SDA.pin1, TURBO/LED.pin2, BOARD/RGB-LEDS.pin2, 4K/L2.pin1, 3K/R2.pin1, Mod1.pin_3, Mod1.pin_8, Mod1.pin_13, Mod1.pin_33, Mod1.pin_38, Mod1.pin_42, LEFT.pin1, START.pin2, 2K/B2.pin1, 1K/B1.pin1, UP.pin1, R3/RS.pin2, LS/TOOGLE.pin2, 1P/3B.pin1, DOWN.pin1, TURBO.pin1, SELECT_2.pin2, A2-TP/CAPTURE.pin2
  N2: 2P/4B.pin2, Mod1.pin_15
  N3: SELECT.pin1, Mod1.pin_21
  N4: RIGHT.pin2, Mod1.pin_6
  N5: A1/HOME.pin1, Mod1.pin_26
  N6: 4P/L1.pin2, Mod1.pin_17
  N7: 3P/R1.pin2, Mod1.pin_16
  N8: RS/TOOGLE.pin1, Mod1.pin_31
  N9: OLED/SCL.pin2, Mod1.pin_2
  N10: OLED/SDA.pin2, Mod1.pin_1
  N11: TURBO/LED.pin1, Mod1.pin_20
  N12: BOARD/RGB-LEDS.pin1, Mod1.pin_34
  N13: 4K/L2.pin2, Mod1.pin_12
  N14: 3K/R2.pin2, Mod1.pin_11
  N15: Mod1.pin_4, UP.pin2
  N16: Mod1.pin_5, DOWN.pin2
  N17: Mod1.pin_7, LEFT.pin2
  N18: Mod1.pin_9, 1K/B1.pin2
  N19: Mod1.pin_10, 2K/B2.pin2
  N20: Mod1.pin_14, 1P/3B.pin2
  N21: Mod1.pin_19, TURBO.pin2
  N22: Mod1.pin_22, START.pin1
  N23: Mod1.pin_24, SELECT_2.pin1
  N24: Mod1.pin_25, R3/RS.pin1
  N25: Mod1.pin_27, A2-TP/CAPTURE.pin1
  N26: Mod1.pin_32, LS/TOOGLE.pin1

custom parts:
  Raspberry Pi Pico: Raspberry Pi Pico. Based around the RP2040 microcontroller the Pico is a low cost microcontroller device bringing Raspberry Pi quality, cost, and easy of use to the microcontroller space. Jan 2021, Split part in to two versions: tht (this one) and SMD. This one will drill holes for a .1 in header in pcb to allow plugging in the module as well as providing pads to solder the module to the top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
